# Fritzing sketch 06_light-powerboost (saved by Fritzing 0.9.3b)
breadboards: 1

parts:
  Mod1 = Raspberry Pi Pico
  GY1 = GY-521 (MPU-6050) [form="♀ (female)" package=THT]
  LED1 = LED - 5mm [color="Red (633nm)" package="5 mm [THT]"]
  R1 = Resistor [tolerance=±5% resistance=220 package=THT]

nets:
  N1: Mod1.pin_3, Mod1.pin_8, Mod1.pin_13, Mod1.pin_18, Mod1.pin_23, Mod1.pin_28, Mod1.pin_33, Mod1.pin_38, Mod1.pin_42, GY1.pin2, R1.Pin_1
  N2: Mod1.pin_17, LED1.anode
  N3: Mod1.pin_19, GY1.pin4
  N4: Mod1.pin_20, GY1.pin3
  N5: Mod1.pin_37, GY1.pin1
  N6: LED1.cathode, R1.Pin_0

custom parts:
  Raspberry Pi Pico: Raspberry Pi Pico. Based around the RP2040 microcontroller the Pico is a low cost microcontroller device bringing Raspberry Pi quality, cost, and easy of use to the microcontroller space. Jan 2021, Split part in to two versions: tht (this one) and SMD. This one will drill holes for a .1 in header in pcb to allow plugging in the module as well as providing pads to solder the module to the top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
  GY-521 (MPU-6050): Placa GY-521 basada en conjunto de acelerómetro+giroscopios MPU-6050
